// Logisim project FU.circ as structural Verilog: 1 circuit, main circuit main
module main (
  input  in_1,
  input  in_2,
  input  in_3,
  input  in_4,
  input  [2:0] Rs,
  input  in_6,
  input  in_7,
  input  in_8,
  input  in_9,
  input  in_10,
  input  MemRead,
  input  [2:0] Rt,
  input  [2:0] Rd2,
  input  [2:0] Rd3,
  input  [2:0] Rd4,
  output [1:0] FA,
  output Stall,
  output [1:0] FB
);

  wire A1, A2, A3, and_7_out, and_8_out, and_9_out, and_10_out, and_11_out, and_12_out, B1, B2, B3,
       comparator_1_eq, comparator_2_eq, comparator_3_eq, comparator_4_eq, comparator_5_eq, comparator_6_eq,
       comparator_7_eq, comparator_8_eq, comparator_9_eq, comparator_10_eq, EX, MEM, NZS, NZT, or_4_out, WB;

  or or_1 (EX, in_1, in_4, in_8);
  or or_2 (MEM, in_2, in_6, in_9);
  or or_3 (WB, in_3, in_7, in_10);
  Comparator #(.width(3), .mode("unsigned")) comparator_1 (.a(Rs), .b(3'b000), .eq(comparator_1_eq));  // open: gt, lt
  not not_1 (NZS, comparator_1_eq);
  Comparator #(.width(3), .mode("unsigned")) comparator_2 (.a(Rs), .b(Rd2), .eq(comparator_2_eq));  // open: gt, lt
  Comparator #(.width(3), .mode("unsigned")) comparator_3 (.a(Rs), .b(Rd3), .eq(comparator_3_eq));  // open: gt, lt
  Comparator #(.width(3), .mode("unsigned")) comparator_4 (.a(Rs), .b(Rd4), .eq(comparator_4_eq));  // open: gt, lt
  not not_2 (NZT, comparator_5_eq);
  Comparator #(.width(3), .mode("unsigned")) comparator_5 (.a(Rt), .b(3'b000), .eq(comparator_5_eq));  // open: gt, lt
  Comparator #(.width(3), .mode("unsigned")) comparator_6 (.a(Rt), .b(Rd2), .eq(comparator_6_eq));  // open: gt, lt
  Comparator #(.width(3), .mode("unsigned")) comparator_7 (.a(Rt), .b(Rd3), .eq(comparator_7_eq));  // open: gt, lt
  Comparator #(.width(3), .mode("unsigned")) comparator_8 (.a(Rt), .b(Rd4), .eq(comparator_8_eq));  // open: gt, lt
  and and_1 (A1, NZS, EX, comparator_2_eq);
  and and_2 (A2, NZS, MEM, comparator_3_eq);
  and and_3 (A3, NZS, WB, comparator_4_eq);
  and and_4 (B1, NZT, EX, comparator_6_eq);
  and and_5 (B2, NZT, MEM, comparator_7_eq);
  and and_6 (B3, NZT, WB, comparator_8_eq);
  and and_7 (and_7_out, ~A1, ~A2, ~A3);  // AND_Gate
  and and_8 (and_8_out, ~A1, ~A2, A3);  // AND_Gate
  and and_9 (and_9_out, ~B1, ~B2, ~B3);  // AND_Gate
  and and_10 (and_10_out, ~B1, ~B2, B3);  // AND_Gate
  and and_11 (and_11_out, ~A1, A2);  // AND_Gate
  and and_12 (and_12_out, ~B1, B2);  // AND_Gate
  Priority_Encoder #(.select(2)) priority_encoder_1 (
    .in0(and_7_out), .in1(A1), .in2(and_11_out), .in3(and_8_out), .out(FA));  // open: gs, en_out, en_in
  Priority_Encoder #(.select(2)) priority_encoder_2 (
    .in0(and_9_out), .in1(B1), .in2(and_12_out), .in3(and_10_out), .out(FB));  // open: gs, en_out, en_in
  Comparator #(.width(2), .mode("unsigned")) comparator_9 (.a(FA), .b(2'b01), .eq(comparator_9_eq));  // open: gt, lt
  Comparator #(.width(2), .mode("unsigned")) comparator_10 (.a(FB), .b(2'b01), .eq(comparator_10_eq));  // open: gt, lt
  or or_4 (or_4_out, comparator_9_eq, comparator_10_eq);
  and and_13 (Stall, or_4_out, MemRead);

  // Other names for the same wires on the sheet: EX_RegW = in_1; ExMN = in_8; ExMZ = in_4; MemMN = in_9; MemMZ = in_6;
  //   MEMRegW = in_2; WbMN = in_10; WbMZ = in_7; WBRegW = in_3
endmodule
