// Logisim project Main & ALU Ctrl.circ as structural Verilog: 1 circuit, main circuit main
module main (
  input  [3:0] op,
  input  [2:0] func,
  input  stall,
  output [3:0] ALUOp,
  output out_5,
  output out_6,
  output out_7,
  output out_8,
  output out_9,
  output out_10,
  output out_11,
  output out_12,
  output out_13,
  output out_14,
  output out_15,
  output out_16
);

  wire main_2_alusrc, main_2_extop, main_2_jal, main_2_jalr, main_2_lui, main_2_memrd, main_2_memwr,
       main_2_movn, main_2_movz, main_2_regwr, main_2_rt, main_2_wbdata;
  wire [3:0] main_1_aluop, stall_t;

  ALUOp_main main_1 (.ALUOp(main_1_aluop), .in_2(op), .func(func));
  and and_1 (out_5, main_2_rt, stall);
  assign ALUOp = stall_t & main_1_aluop;  // AND_Gate and_2, 4 bits wide
  and and_3 (out_7, main_2_extop, stall);
  and and_4 (out_6, main_2_regwr, stall);
  and and_5 (out_9, main_2_memrd, stall);
  and and_6 (out_8, main_2_alusrc, stall);
  and and_7 (out_11, main_2_wbdata, stall);
  and and_8 (out_10, main_2_memwr, stall);
  MainCtrl_main main_2 (
    .in_1(op), .in_2(func), .RT(main_2_rt), .RegWr(main_2_regwr), .ExtOp(main_2_extop),
    .ALUSrc(main_2_alusrc), .MemRd(main_2_memrd), .MemWr(main_2_memwr), .WBdata(main_2_wbdata),
    .JAL(main_2_jal), .JALR(main_2_jalr), .Lui(main_2_lui), .MOVZ(main_2_movz), .MOVN(main_2_movn));
  and and_9 (out_13, main_2_jalr, stall);
  and and_10 (out_12, main_2_jal, stall);
  and and_11 (out_15, main_2_movz, stall);
  and and_12 (out_14, main_2_lui, stall);
  and and_13 (out_16, main_2_movn, stall);
  assign stall_t = {{3{stall}}, stall};  // Bit_Extender bit_extender_1
endmodule
