// Logisim project MainCtrl.circ as structural Verilog: 1 circuit, main circuit main
module main (
  input  [3:0] in_1,
  input  [2:0] in_2,
  output ExtOp,
  output ALUSrc,
  output RT,
  output RegWr,
  output MemRd,
  output MemWr,
  output WBdata,
  output JAL,
  output JALR,
  output Lui,
  output MOVZ,
  output MOVN
);

  wire _0001, and_1_out, decoder_1_out0, decoder_1_out2, decoder_1_out3, decoder_1_out4, decoder_1_out7,
       decoder_1_out8, decoder_1_out9, decoder_1_out10, decoder_1_out11, decoder_1_out12, jalr_t, jr, movn_t,
       movz_t, or_2_out;

  Decoder #(.select(4), .enable("false")) decoder_1 (
    .out0(decoder_1_out0), .out1(_0001), .out2(decoder_1_out2), .out3(decoder_1_out3), .out4(decoder_1_out4),
    .out5(MemWr), .out6(MemRd), .out7(decoder_1_out7), .out8(decoder_1_out8), .out9(decoder_1_out9),
    .out10(decoder_1_out10), .out11(decoder_1_out11), .out12(decoder_1_out12), .out13(Lui), .out15(JAL),
    .sel(in_1));  // open: out14
  or or_1 (RT, MemWr, or_2_out);
  or or_2 (or_2_out, decoder_1_out7, decoder_1_out8, decoder_1_out9, decoder_1_out10, decoder_1_out11, decoder_1_out12);
  and and_1 (and_1_out, ~jr, ~movz_t, ~movn_t, _0001);  // AND_Gate
  or or_3 (RegWr, decoder_1_out0, and_1_out, decoder_1_out2, decoder_1_out3, decoder_1_out4, MemRd, Lui, JAL);
  nor nor_1 (ExtOp, decoder_1_out2, decoder_1_out3);
  nor nor_2 (ALUSrc, decoder_1_out0, or_2_out, _0001);
  Decoder #(.select(3), .enable("false")) decoder_2 (
    .out4(movz_t), .out5(movn_t), .out6(jr), .out7(jalr_t), .sel(in_2));  // open: out0, out1, out2, out3
  and and_2 (JALR, jalr_t, _0001);
  and and_3 (MOVZ, movz_t, _0001);
  and and_4 (MOVN, movn_t, _0001);

  assign WBdata = MemRd;

  // Other names for the same wires on the sheet: func[2:0] = in_2; op[3:0] = in_1
endmodule
