// Logisim project file_reg.circ as structural Verilog: 4 circuits, main circuit File Reg
module main (
  output [15:0] out_1,
  output [15:0] out_2,
  output [15:0] out_3,
  output [15:0] out_4,
  output [15:0] out_5,
  output [15:0] out_6,
  output [15:0] out_7,
  output [1:0] out_8,
  output [1:0] out_9,
  output [2:0] out_10,
  output [3:0] out_11
);

  wire ALUSrc, and_1_out, and_2_out, and_3_out, clk, CtrlJAL, CtrlJALR, CtrlLUI, CtrlMemRd, CtrlMemWr,
       CtrlMOVN, CtrlMOVZ, CtrlWBdata, ExALUSrc, ExLUI, ExMemRd, ExMN_FU, ExMOVN, ExMOVZ, ExMZ_FU, EXRegWr,
       ExRTZ, ExtOp, GT, main_1_stall, MemJAL, MemJALR, MemMN_FU, MemMOVN, MemMOVZ, MemMZ_FU, MemRd,
       MemRegWr, MemRTZ, MemWr, or_1_out, or_2_out, pc_ctrl_1_kill1, pc_ctrl_1_kill2, RegWr, RT, stall,
       WBdata, WbMN_FU, WbMOVN, WbMOVZ, WbMZ_FU, WBRegWr, WbRTZ, Zero;
  wire [2:0] func, func_delayed, multiplexer_4_out, multiplexer_5_out, RD2, RD3, RD4, Rs, Rt_t;
  wire [3:0] ALUOp, op_delayed, register_3_q_2;
  wire [11:0] A_2_q, A_3_q, A_q, adder_2_out, bit_extender_2_out, multiplexer_1_out, pc1, register_1_q;
  wire [11:3] EX_q, register_3_q;
  wire [15:0] A_4_q, ALU, B, bit_extender_1_out, bit_extender_3_out, D_q, extender_1_imm16, file_reg_1_busa,
       file_reg_1_busb, Imm16, LUI_Imm12, MEM, multiplexer_2_out, multiplexer_6_out, multiplexer_7_out,
       multiplexer_8_out, multiplexer_9_out, multiplexer_10_out, multiplexer_11_out, multiplexer_12_out, R_q,
       ram_1_data, register_7_q, register_8_q, Result, rom_1_data;
  wire [15:2] MEM_q, WB_q;

  Multiplexer #(.select(3), .width(12), .enable("false")) multiplexer_1 (
    .in0(pc1), .in1(A_q), .in2(A_3_q), .in3(file_reg_1_busa[11:0]), .in4(file_reg_1_busa[11:0]),
    .out(multiplexer_1_out), .sel(out_10));  // open: in5, in6, in7
  pc_ctrl pc_ctrl_1 (
    .Op(op_delayed), .in_2(Zero), .in_3(GT), .in_4(func_delayed), .PCsrc(out_10), .kill1(pc_ctrl_1_kill1),
    .kill2(pc_ctrl_1_kill2));
  FU_main main_1 (
    .Rs(Rs), .MemRead(ExMemRd), .Rt(Rt_t), .Rd2(RD2), .Rd3(RD3), .Rd4(RD4), .Stall(main_1_stall),
    .in_1(EXRegWr), .in_3(WBRegWr), .in_2(MemRegWr), .FA(out_8), .FB(out_9), .in_4(ExMZ_FU), .in_6(MemMZ_FU),
    .in_7(WbMZ_FU), .in_8(ExMN_FU), .in_9(MemMN_FU), .in_10(WbMN_FU));
  Adder #(.width(12)) adder_1 (.a(12'h1), .b(register_1_q), .out(pc1));  // open: cin, cout
  Register #(.width(12)) register_1 (.D(multiplexer_1_out), .en(stall), .Q(register_1_q), .clk(clk));  // open: clr
  not not_1 (stall, main_1_stall);
  Clock clock_1 (.out(clk));
  Register #(.width(12)) A (
    .D({register_3_q[11:9], Rs, register_3_q[5:3], func}), .en(stall), .Q(A_q), .clk(clk));  // open: clr
  Register #(.width(12)) A_2 (.D(register_1_q), .en(stall), .Q(A_2_q), .clk(clk));  // open: clr
  ROM #(.addrWidth(12), .dataWidth(16)) rom_1 (.addr(register_1_q), .data(rom_1_data), .sel(stall));
  Register #(.width(4)) register_2 (.D(register_3_q_2), .Q(op_delayed), .clk(clk));  // open: en, clr
  Multiplexer #(.width(16), .enable("false")) multiplexer_2 (
    .in0(rom_1_data), .in1({16{1'b0}}), .out(multiplexer_2_out), .sel(pc_ctrl_1_kill1));
  Register #(.width(16)) register_3 (
    .D(multiplexer_2_out), .en(stall), .Q({register_3_q_2, register_3_q[11:9], Rs, register_3_q[5:3], func}),
    .clk(clk));  // open: clr
  assign bit_extender_1_out = {{4{1'b0}}, {register_3_q[11:9], Rs, register_3_q[5:3], func}};  // Bit_Extender bit_extender_1
  Multiplexer #(.width(3), .enable("false")) multiplexer_3 (
    .in0(register_3_q[5:3]), .in1(register_3_q[11:9]), .out(Rt_t), .sel(RT));
  Multiplexer #(.width(3), .enable("false")) multiplexer_4 (
    .in0(register_3_q[11:9]), .in1(3'b111), .out(multiplexer_4_out), .sel(CtrlJAL));
  and and_1 (and_1_out, ~pc_ctrl_1_kill2, stall);  // AND_Gate
  Register #(.width(16)) register_4 (.D(bit_extender_1_out), .Q(LUI_Imm12), .clk(clk));  // open: en, clr
  Multiplexer #(.width(3), .enable("false")) multiplexer_5 (
    .in0(multiplexer_4_out), .in1(3'b001), .out(multiplexer_5_out), .sel(CtrlLUI));
  and and_2 (and_2_out, WbRTZ, WbMOVZ);
  and and_3 (and_3_out, ~WbRTZ, WbMOVN);  // AND_Gate
  Main___ALU_Ctrl_main main_2 (
    .op(register_3_q_2), .func(func), .ALUOp(out_11), .stall(and_1_out), .out_5(RT), .out_6(RegWr),
    .out_7(ExtOp), .out_8(ALUSrc), .out_9(CtrlMemRd), .out_10(CtrlMemWr), .out_11(CtrlWBdata),
    .out_12(CtrlJAL), .out_13(CtrlJALR), .out_14(CtrlLUI), .out_15(CtrlMOVZ), .out_16(CtrlMOVN));
  Register #(.width(3)) register_5 (.D(func), .Q(func_delayed), .clk(clk));  // open: en, clr
  File_Reg file_reg_1 (
    .RA(Rs), .RB(Rt_t), .RW(RD4), .RegWrite(or_1_out), .BusW(Result), .BusA(file_reg_1_busa),
    .BusB(file_reg_1_busb), .Clock(clk), .out_15(out_5), .out_14(out_7), .out_11(out_4), .out_10(out_2),
    .out_9(out_6), .out_8(out_3), .out_7(out_1));
  or or_1 (or_1_out, and_2_out, and_3_out, WBRegWr);
  assign bit_extender_2_out = {{6{register_3_q[5]}}, {register_3_q[5:3], func}};  // Bit_Extender bit_extender_2
  extender extender_1 (.Imm6({register_3_q[5:3], func}), .Imm16(extender_1_imm16), .ExtOp(ExtOp));
  Adder #(.width(12)) adder_2 (.a(A_2_q), .b(bit_extender_2_out), .out(adder_2_out));  // open: cin, cout
  Multiplexer #(.select(2), .width(16), .enable("false")) multiplexer_6 (
    .in0(file_reg_1_busa), .in1(ALU), .in2(MEM), .in3(Result), .out(multiplexer_6_out), .sel(out_8));
  Multiplexer #(.select(2), .width(16), .enable("false")) multiplexer_7 (
    .in0(file_reg_1_busb), .in1(ALU), .in2(MEM), .in3(Result), .out(multiplexer_7_out), .sel(out_9));
  Register #(.width(16)) register_6 (.D(extender_1_imm16), .Q(Imm16), .clk(clk));  // open: en, clr
  Register #(.width(12)) A_3 (.D(adder_2_out), .Q(A_3_q), .clk(clk));  // open: en, clr
  Register #(.width(16)) A_4 (.D(multiplexer_6_out), .Q(A_4_q), .clk(clk));  // open: en, clr
  Register #(.width(16)) u_B (.D(multiplexer_7_out), .Q(B), .clk(clk));  // open: en, clr
  Register #(.width(3)) u_RD2 (.D(multiplexer_5_out), .Q(RD2), .clk(clk));  // open: en, clr
  Multiplexer #(.width(16), .enable("false")) multiplexer_8 (
    .in0(A_4_q), .in1(LUI_Imm12), .out(multiplexer_8_out), .sel(ExLUI));
  Multiplexer #(.width(16), .enable("false")) multiplexer_9 (
    .in0(B), .in1(Imm16), .out(multiplexer_9_out), .sel(ExALUSrc));
  Comparator #(.width(16)) comparator_1 (.a(B), .b({16{1'b0}}), .eq(ExRTZ));  // open: gt, lt
  Multiplexer #(.width(16), .enable("false")) multiplexer_10 (
    .in0(multiplexer_9_out), .in1(16'h4), .out(multiplexer_10_out), .sel(ExLUI));
  Register #(.width(16)) register_7 (.D(B), .Q(register_7_q), .clk(clk));  // open: en, clr
  assign bit_extender_3_out = {{4{1'b0}}, pc1};  // Bit_Extender bit_extender_3
  Multiplexer #(.width(16), .enable("false")) multiplexer_11 (
    .in0(multiplexer_10_out), .in1({16{1'b0}}), .out(multiplexer_11_out), .sel(ExMOVN));
  Register #(.width(16)) EX (
    .D({out_11, RT, RegWr, ExtOp, ALUSrc, CtrlMemRd, CtrlMemWr, CtrlWBdata, CtrlJAL, CtrlJALR, CtrlLUI, CtrlMOVZ, CtrlMOVN}),
    .Q({ALUOp, EX_q[11], EXRegWr, EX_q[9], ExALUSrc, ExMemRd, EX_q[6:3], ExLUI, ExMOVZ, ExMOVN}), .clk(clk));  // open: en, clr
  Register #(.width(16)) register_8 (.D(register_7_q), .Q(register_8_q), .clk(clk));  // open: en, clr
  Comparator #(.width(16)) comparator_2 (.a(register_7_q), .b({16{1'b0}}), .eq(MemRTZ));  // open: gt, lt
  ALU_main main_3 (
    .DATA_A(multiplexer_8_out), .DATA_B(multiplexer_11_out), .ALUOp(ALUOp), .GT(GT), .ZERO(Zero), .RESULT(ALU));
  Comparator #(.width(16)) comparator_3 (.a(register_8_q), .b({16{1'b0}}), .eq(WbRTZ));  // open: gt, lt
  Register #(.width(3)) u_RD3 (.D(RD2), .Q(RD3), .clk(clk));  // open: en, clr
  Register #(.width(16)) R (.D(ALU), .Q(R_q), .clk(clk));  // open: en, clr
  Register #(.width(16)) D (.D(B), .Q(D_q), .clk(clk));  // open: en, clr
  and and_4 (ExMZ_FU, ExRTZ, ExMOVZ);
  and and_5 (MemMZ_FU, MemRTZ, MemMOVZ);
  and and_6 (WbMZ_FU, WbRTZ, WbMOVZ);
  and and_7 (ExMN_FU, ~ExRTZ, ExMOVN);  // AND_Gate
  and and_8 (MemMN_FU, ~MemRTZ, MemMOVN);  // AND_Gate
  and and_9 (WbMN_FU, ~WbRTZ, WbMOVN);  // AND_Gate
  Register #(.width(16)) u_MEM (
    .D({ALUOp, EX_q[11], EXRegWr, EX_q[9], ExALUSrc, ExMemRd, EX_q[6:3], ExLUI, ExMOVZ, ExMOVN}),
    .Q({MEM_q[15:11], MemRegWr, MEM_q[9:8], MemRd, MemWr, WBdata, MemJAL, MemJALR, MEM_q[2], MemMOVZ, MemMOVN}),
    .clk(clk));  // open: en, clr
  RAM #(.addrWidth(12), .dataWidth(16), .bus("separate")) ram_1 (
    .addr(R_q[11:0]), .din(D_q), .data(ram_1_data), .str(MemWr), .clk(clk), .ld(MemRd));  // open: sel, clr
  Multiplexer #(.width(16), .enable("false")) multiplexer_12 (
    .in0(R_q), .in1(ram_1_data), .out(multiplexer_12_out), .sel(WBdata));
  Multiplexer #(.width(16), .enable("false")) multiplexer_13 (
    .in0(multiplexer_12_out), .in1(bit_extender_3_out), .out(MEM), .sel(or_2_out));
  or or_2 (or_2_out, MemJAL, MemJALR);
  Register #(.width(16)) DATA (.D(MEM), .Q(Result), .clk(clk));  // open: en, clr
  Register #(.width(16)) WB (
    .D({MEM_q[15:11], MemRegWr, MEM_q[9:8], MemRd, MemWr, WBdata, MemJAL, MemJALR, MEM_q[2], MemMOVZ, MemMOVN}),
    .Q({WB_q[15:11], WBRegWr, WB_q[9:2], WbMOVZ, WbMOVN}), .clk(clk));  // open: en, clr
  Register #(.width(3)) u_RD4 (.D(RD3), .Q(RD4), .clk(clk));  // open: en, clr

  // Other names for the same wires on the sheet: FA[1:0] = out_8; FB[1:0] = out_9; R1[15:0] = out_1; R2[15:0] = out_3;
  //   R3[15:0] = out_6; R4[15:0] = out_2; R5[15:0] = out_4; R6[15:0] = out_7; R7[15:0] = out_5

  // Notes on the sheet:
  //   PC = PC + 1
  //   PC = RS[11:0]
  //   PC = Branch Target
  //   PC = Imm12
  //   contents of rom_1 (hex, n*v repeats v):
  //   d003 1444 467f 1854 ac8 cc9 eca 5200 5401 5602 5803 5a04 5c05 5e06 4e1f 29b 5bc 7f5 8c6 a1e cc7 e1f
  //   5207 5408 5609 580a 5a0b 5c0c 5e0d 12f0 14f1 17bd 18f2 1bb3 1ccd 2ec3 520e 540f 5610 5811 5a12 5c13
  //   5e14 3a41 38bf 22fe 6dff 5215 5816 5a17 5c18 4200 4402 4600 4804 4a00 4c06 4e06
  //   Op
  //   RD
  //   RT
  //   Imm12
  //   RS
  //   RT
  //   JAL
  //   LUI
  //   Imm6
  //   RegWr
  //   ALU Result
  //   MemWr
  //   MemRd
  //   WBData
endmodule

module File_Reg (
  input  [2:0] RA,
  input  [2:0] RB,
  input  [2:0] RW,
  input  RegWrite,
  input  Clock,
  input  [15:0] BusW,
  output [15:0] out_7,
  output [15:0] out_8,
  output [15:0] out_9,
  output [15:0] out_10,
  output [15:0] out_11,
  output [15:0] BusA,
  output [15:0] BusB,
  output [15:0] out_14,
  output [15:0] out_15
);

  wire and_1_out, and_2_out, and_3_out, and_4_out, and_5_out, and_6_out, and_7_out, decoder_1_out0,
       decoder_1_out1, decoder_1_out2, decoder_1_out3, decoder_1_out4, decoder_1_out5, decoder_1_out6,
       decoder_1_out7, decoder_2_out0, decoder_2_out1, decoder_2_out2, decoder_2_out3, decoder_2_out4,
       decoder_2_out5, decoder_2_out6, decoder_2_out7, decoder_3_out0, decoder_3_out1, decoder_3_out2,
       decoder_3_out3, decoder_3_out4, decoder_3_out5, decoder_3_out6, decoder_3_out7;

  Decoder #(.select(3), .enable("false")) decoder_1 (
    .out0(decoder_1_out0), .out1(decoder_1_out1), .out2(decoder_1_out2), .out3(decoder_1_out3),
    .out4(decoder_1_out4), .out5(decoder_1_out5), .out6(decoder_1_out6), .out7(decoder_1_out7), .sel(RW));
  and and_1 (and_1_out, decoder_1_out1, RegWrite);
  and and_2 (and_2_out, decoder_1_out2, RegWrite);
  and and_3 (and_3_out, decoder_1_out3, RegWrite);
  and and_4 (and_4_out, decoder_1_out4, RegWrite);
  and and_5 (and_5_out, decoder_1_out5, RegWrite);
  and and_6 (and_6_out, decoder_1_out6, RegWrite);
  and and_7 (and_7_out, decoder_1_out7, RegWrite);
  Register #(.width(16)) register_1 (.D(BusW), .en(and_1_out), .Q(out_7), .clk(Clock));  // open: clr
  Register #(.width(16)) register_2 (.D(BusW), .en(and_2_out), .Q(out_8), .clk(Clock));  // open: clr
  Register #(.width(16)) register_3 (.D(BusW), .en(and_3_out), .Q(out_9), .clk(Clock));  // open: clr
  Register #(.width(16)) register_4 (.D(BusW), .en(and_4_out), .Q(out_10), .clk(Clock));  // open: clr
  Register #(.width(16)) register_5 (.D(BusW), .en(and_5_out), .Q(out_11), .clk(Clock));  // open: clr
  Register #(.width(16)) register_6 (.D(BusW), .en(and_6_out), .Q(out_14), .clk(Clock));  // open: clr
  Register #(.width(16)) register_7 (.D(BusW), .en(and_7_out), .Q(out_15), .clk(Clock));  // open: clr
  Decoder #(.select(3), .enable("false")) decoder_2 (
    .out0(decoder_2_out0), .out1(decoder_2_out1), .out2(decoder_2_out2), .out3(decoder_2_out3),
    .out4(decoder_2_out4), .out5(decoder_2_out5), .out6(decoder_2_out6), .out7(decoder_2_out7), .sel(RA));
  assign BusA = decoder_2_out1 ? out_7 : 16'bz;  // Controlled_Buffer controlled_buffer_1
  assign BusA = decoder_2_out2 ? out_8 : 16'bz;  // Controlled_Buffer controlled_buffer_2
  assign BusA = decoder_2_out3 ? out_9 : 16'bz;  // Controlled_Buffer controlled_buffer_3
  assign BusA = decoder_2_out4 ? out_10 : 16'bz;  // Controlled_Buffer controlled_buffer_4
  assign BusA = decoder_2_out5 ? out_11 : 16'bz;  // Controlled_Buffer controlled_buffer_5
  assign BusA = decoder_2_out6 ? out_14 : 16'bz;  // Controlled_Buffer controlled_buffer_6
  assign BusA = decoder_2_out7 ? out_15 : 16'bz;  // Controlled_Buffer controlled_buffer_7
  assign BusA = decoder_2_out0 ? {16{1'b0}} : 16'bz;  // Controlled_Buffer controlled_buffer_8
  Decoder #(.select(3), .enable("false")) decoder_3 (
    .out0(decoder_3_out0), .out1(decoder_3_out1), .out2(decoder_3_out2), .out3(decoder_3_out3),
    .out4(decoder_3_out4), .out5(decoder_3_out5), .out6(decoder_3_out6), .out7(decoder_3_out7), .sel(RB));
  assign BusB = decoder_3_out2 ? out_8 : 16'bz;  // Controlled_Buffer controlled_buffer_9
  assign BusB = decoder_3_out3 ? out_9 : 16'bz;  // Controlled_Buffer controlled_buffer_10
  assign BusB = decoder_3_out4 ? out_10 : 16'bz;  // Controlled_Buffer controlled_buffer_11
  assign BusB = decoder_3_out5 ? out_11 : 16'bz;  // Controlled_Buffer controlled_buffer_12
  assign BusB = decoder_3_out6 ? out_14 : 16'bz;  // Controlled_Buffer controlled_buffer_13
  assign BusB = decoder_3_out7 ? out_15 : 16'bz;  // Controlled_Buffer controlled_buffer_14
  assign BusB = decoder_3_out0 ? {16{1'b0}} : 16'bz;  // Controlled_Buffer controlled_buffer_15
  assign BusB = decoder_3_out1 ? out_7 : 16'bz;  // Controlled_Buffer controlled_buffer_16
endmodule

module extender (
  input  [5:0] Imm6,
  input  ExtOp,
  output [15:0] Imm16
);

  wire [15:0] bit_extender_1_out, bit_extender_2_out;

  assign bit_extender_1_out = {{10{1'b0}}, Imm6};  // Bit_Extender bit_extender_1
  assign bit_extender_2_out = {{10{Imm6[5]}}, Imm6};  // Bit_Extender bit_extender_2
  Multiplexer #(.width(16), .enable("false")) multiplexer_1 (
    .in0(bit_extender_1_out), .in1(bit_extender_2_out), .out(Imm16), .sel(ExtOp));
endmodule

module pc_ctrl (
  input  [3:0] Op,
  input  in_2,
  input  in_3,
  input  [2:0] in_4,
  output [2:0] PCsrc,
  output kill2,
  output kill1
);

  wire _0, _2, _3, _4, _5, _6, _13, and_3_out, BEQ_out, BGE_out, BGT_out, BLE_out, BLT_out, BNE_out,
       decoder_1_out1, decoder_1_out7, decoder_1_out8, decoder_1_out9, decoder_1_out10, decoder_1_out11,
       decoder_1_out12, decoder_1_out14, decoder_1_out15, JALR, JALROUT, JR, JROUT, or_1_out, or_2_out,
       or_5_out;

  Decoder #(.select(4), .enable("false")) decoder_1 (
    .out0(_0), .out1(decoder_1_out1), .out2(_2), .out3(_3), .out4(_4), .out5(_5), .out6(_6),
    .out7(decoder_1_out7), .out8(decoder_1_out8), .out9(decoder_1_out9), .out10(decoder_1_out10),
    .out11(decoder_1_out11), .out12(decoder_1_out12), .out13(_13), .out14(decoder_1_out14),
    .out15(decoder_1_out15), .sel(Op));
  and and_1 (JR, ~in_4[0], in_4[1], in_4[2]);  // AND_Gate
  and and_2 (JALR, in_4[0], in_4[1], in_4[2]);
  or or_1 (or_1_out, in_2, in_3);
  and and_3 (and_3_out, ~in_2, ~in_3);  // AND_Gate
  and BNE (BNE_out, decoder_1_out7, ~in_2);  // AND_Gate
  and BEQ (BEQ_out, decoder_1_out8, in_2);
  and BGT (BGT_out, decoder_1_out9, in_3);
  and BGE (BGE_out, decoder_1_out10, or_1_out);
  and BLT (BLT_out, decoder_1_out11, and_3_out);
  and BLE (BLE_out, decoder_1_out12, ~in_3);  // AND_Gate
  or or_2 (or_2_out, decoder_1_out14, decoder_1_out15);
  or or_3 (kill2, BNE_out, BEQ_out, BGT_out, BGE_out, BLT_out, BLE_out);
  and and_4 (JROUT, decoder_1_out1, JR);
  and and_5 (JALROUT, decoder_1_out1, JALR);
  or or_4 (kill1, kill2, JROUT, JALROUT, or_2_out);
  or or_5 (or_5_out, _0, _2, ~JROUT, ~JALROUT, _3, _4, _5, _6, _13);  // OR_Gate
  Priority_Encoder priority_encoder_1 (
    .in0(or_5_out), .in1(or_2_out), .in2(kill2), .in3(JROUT), .in4(JALROUT), .out(PCsrc));  // open: in5, in6, in7, en_in, gs, en_out

  // Other names for the same wires on the sheet: func[2:0] = in_4; GT = in_3; zero = in_2
endmodule
