// Logisim project ALU.circ as structural Verilog: 1 circuit, main circuit main
module main (
  input  [15:0] DATA_A,
  input  [15:0] DATA_B,
  input  [3:0] ALUOp,
  output GT,
  output ZERO,
  output [15:0] RESULT
);

  wire comparator_2_eq, comparator_2_gt, or_2_out, or_3_out;
  wire [15:0] adder_1_out, and_1_out, bit_extender_1_out, bit_extender_2_out, not_1_out, or_1_out,
       shifter_1_out, shifter_2_out, shifter_3_out, shifter_4_out, subtractor_1_out, xor_1_out;

  Shifter #(.width(16)) shifter_1 (.in(DATA_A), .\dist (DATA_B[3:0]), .out(shifter_1_out));
  Shifter #(.width(16), .shift("lr")) shifter_2 (.in(DATA_A), .\dist (DATA_B[3:0]), .out(shifter_2_out));
  Shifter #(.width(16), .shift("ar")) shifter_3 (.in(DATA_A), .\dist (DATA_B[3:0]), .out(shifter_3_out));
  Shifter #(.width(16), .shift("rr")) shifter_4 (.in(DATA_A), .\dist (DATA_B[3:0]), .out(shifter_4_out));
  assign xor_1_out = DATA_A ^ DATA_B;  // XOR_Gate xor_1, 16 bits wide
  assign and_1_out = DATA_A & DATA_B;  // AND_Gate and_1, 16 bits wide
  assign or_1_out = DATA_A | DATA_B;  // OR_Gate or_1, 16 bits wide
  Comparator #(.width(16)) comparator_1 (.a(DATA_A), .b(DATA_B), .gt(GT), .eq(ZERO));  // open: lt
  Comparator #(.width(16), .mode("unsigned")) comparator_2 (
    .a(DATA_A), .b(DATA_B), .gt(comparator_2_gt), .eq(comparator_2_eq));  // open: lt
  Adder #(.width(16)) adder_1 (.a(DATA_A), .b(DATA_B), .out(adder_1_out));  // open: cin, cout
  Subtractor #(.width(16)) subtractor_1 (.a(DATA_A), .b(DATA_B), .out(subtractor_1_out));  // open: bin, bout
  assign not_1_out = ~and_1_out;  // NOT_Gate not_1, 16 bits wide
  or or_2 (or_2_out, GT, ZERO);
  or or_3 (or_3_out, comparator_2_gt, comparator_2_eq);
  assign bit_extender_1_out = {{15{1'b0}}, or_2_out};  // Bit_Extender bit_extender_1
  assign bit_extender_2_out = {{15{1'b0}}, or_3_out};  // Bit_Extender bit_extender_2
  Multiplexer #(.select(4), .width(16), .enable("false")) multiplexer_1 (
    .in0(or_1_out), .in1(and_1_out), .in2(not_1_out), .in3(xor_1_out), .in4(adder_1_out),
    .in5(subtractor_1_out), .in6(bit_extender_1_out), .in7(bit_extender_2_out), .in8(shifter_1_out),
    .in9(shifter_2_out), .in10(shifter_3_out), .in11(shifter_4_out), .in15(shifter_1_out), .out(RESULT),
    .sel(ALUOp));  // open: in12, in13, in14

  // Notes on the sheet:
  //   ADD
  //   SUB
endmodule
