// Logisim project ALUOp.circ as structural Verilog: 1 circuit, main circuit main
// OP's LSB
module main (
  input  [2:0] func,
  input  [3:0] in_2,
  output [3:0] ALUOp
);

  wire ADD, AND, and_1_out, and_2_out, and_5_out, and_6_out, and_7_out, and_8_out, and_9_out, and_10_out,
       not_1_out, not_2_out, not_3_out, not_4_out, not_5_out, not_6_out, not_7_out, not_8_out, not_9_out,
       not_10_out, not_11_out, not_12_out, not_13_out, not_14_out, not_16_out, not_17_out, OR, or_4_out, R,
       SLL;
  wire [3:0] bit_extender_1_out, bit_extender_2_out, bit_extender_3_out, IM, multiplexer_2_out,
       multiplexer_3_out, multiplexer_5_out, multiplexer_6_out, not_15_out, or_3_out, shifter_1_out;

  and and_1 (and_1_out, ~in_2[3], ~in_2[2], ~in_2[1], ~in_2[0]);  // AND_Gate
  and and_2 (and_2_out, ~in_2[3], ~in_2[2], ~in_2[1], in_2[0]);  // AND_Gate
  or or_1 (R, and_1_out, and_2_out);
  not not_1 (not_1_out, in_2[1]);
  not not_2 (not_2_out, in_2[0]);
  not not_3 (not_3_out, in_2[2]);
  not not_4 (not_4_out, in_2[3]);
  and and_3 (SLL, in_2[0], not_1_out, in_2[2], in_2[3]);
  and and_4 (AND, not_2_out, in_2[1], not_3_out, not_4_out);
  assign bit_extender_1_out = {{1{1'b0}}, func};  // Bit_Extender bit_extender_1
  not not_5 (not_5_out, func[1]);
  not not_6 (not_6_out, in_2[0]);
  not not_7 (not_7_out, in_2[2]);
  and and_5 (and_5_out, not_6_out, in_2[1], not_7_out, not_8_out);
  not not_8 (not_8_out, in_2[3]);
  not not_9 (not_9_out, in_2[0]);
  and and_6 (and_6_out, not_9_out, in_2[1], not_10_out, in_2[3]);
  not not_10 (not_10_out, in_2[2]);
  not not_11 (not_11_out, in_2[0]);
  and and_7 (and_7_out, not_11_out, in_2[1], in_2[2], not_12_out);
  not not_12 (not_12_out, in_2[3]);
  not not_13 (not_13_out, in_2[1]);
  Shifter #(.width(4)) shifter_1 (.in(in_2), .\dist (2'b11), .out(shifter_1_out));
  not not_14 (not_14_out, func[0]);
  or or_2 (ADD, and_5_out, and_6_out, and_7_out);
  and and_8 (and_8_out, in_2[3], in_2[2], not_13_out, in_2[0]);
  and and_9 (and_9_out, func[2], not_5_out, in_2[0], func[0]);
  and and_10 (and_10_out, func[2], in_2[0], not_5_out, not_14_out);
  assign bit_extender_2_out = {{3{and_8_out}}, and_8_out};  // Bit_Extender bit_extender_2
  assign or_3_out = shifter_1_out | bit_extender_1_out;  // OR_Gate or_3, 4 bits wide
  or or_4 (or_4_out, and_9_out, and_10_out);
  Multiplexer #(.width(4), .enable("false")) multiplexer_1 (.in0(IM), .in1(multiplexer_2_out), .out(ALUOp), .sel(R));
  Multiplexer #(.width(4), .enable("false")) multiplexer_2 (
    .in0(multiplexer_3_out), .in1(not_15_out), .out(multiplexer_2_out), .sel(or_4_out));
  Multiplexer #(.width(4), .enable("false")) multiplexer_3 (
    .in0(or_3_out), .in1(bit_extender_2_out), .out(multiplexer_3_out), .sel(and_8_out));
  assign not_15_out = ~bit_extender_3_out;  // NOT_Gate not_15, 4 bits wide
  assign bit_extender_3_out = {{3{or_4_out}}, or_4_out};  // Bit_Extender bit_extender_3
  not not_16 (not_16_out, in_2[2]);
  and and_11 (OR, in_2[0], in_2[1], not_16_out, not_17_out);
  not not_17 (not_17_out, in_2[3]);
  Multiplexer #(.width(4), .enable("false")) multiplexer_4 (.in0(multiplexer_5_out), .in1(4'b0000), .out(IM), .sel(OR));
  Multiplexer #(.width(4), .enable("false")) multiplexer_5 (
    .in0(multiplexer_6_out), .in1(4'b1000), .out(multiplexer_5_out), .sel(SLL));
  Multiplexer #(.width(4), .enable("false")) multiplexer_6 (
    .in0(4'b0100), .in1(4'b0001), .out(multiplexer_6_out), .sel(AND));

  // Other names for the same wires on the sheet: OP[3:0] = in_2; OP_s_LSB = in_2[0]
endmodule
