// Logisim project file_reg.circ as structural Verilog: 4 circuits, main circuit File Reg
module main (
  output [15:0] out_1,
  output [15:0] out_2,
  output [15:0] out_3,
  output [15:0] out_4,
  output [15:0] out_5,
  output [15:0] out_6,
  output [15:0] out_7
);

  wire ALUSrc, and_1_out, and_2_out, clock_1_out, ExtOp, GT, JAL, JALR, LUI, MemRd, MemWr, MOVN, MOVZ,
       or_1_out, or_2_out, RegWr, RT, RTZ, WBdata, Zero;
  wire [2:0] func, multiplexer_2_out, multiplexer_3_out, multiplexer_4_out, pc_ctrl_1_pcsrc;
  wire [3:0] main_2_aluop, rom_1_data_2;
  wire [11:0] adder_2_out, bit_extender_2_out, multiplexer_1_out, pc1, register_1_q;
  wire [11:3] rom_1_data;
  wire [15:0] bit_extender_3_out, file_reg_1_busa, file_reg_1_busb, Imm16, LUI_Imm12, main_3_result,
       multiplexer_5_out, multiplexer_6_out, multiplexer_7_out, multiplexer_8_out, multiplexer_9_out,
       ram_1_data, Result;

  Multiplexer #(.select(3), .width(12), .enable("false")) multiplexer_1 (
    .in0(pc1), .in1({rom_1_data, func}), .in2(adder_2_out), .in3(file_reg_1_busa[11:0]),
    .in4(file_reg_1_busa[11:0]), .out(multiplexer_1_out), .sel(pc_ctrl_1_pcsrc));  // open: in5, in6, in7
  pc_ctrl pc_ctrl_1 (.Op(rom_1_data_2), .in_2(Zero), .in_3(GT), .in_4(func), .PCsrc(pc_ctrl_1_pcsrc));
  Clock clock_1 (.out(clock_1_out));
  Register #(.width(12)) register_1 (.D(multiplexer_1_out), .Q(register_1_q), .clk(clock_1_out));  // open: en, clr
  Adder #(.width(12)) adder_1 (.a(12'h1), .b(register_1_q), .out(pc1));  // open: cin, cout
  ROM #(.addrWidth(12), .dataWidth(16)) rom_1 (
    .addr(register_1_q), .data({rom_1_data_2, rom_1_data, func}));  // open: sel
  assign LUI_Imm12 = {{4{1'b0}}, {rom_1_data, func}};  // Bit_Extender bit_extender_1
  Multiplexer #(.width(3), .enable("false")) multiplexer_2 (
    .in0(rom_1_data[5:3]), .in1(rom_1_data[11:9]), .out(multiplexer_2_out), .sel(RT));
  Multiplexer #(.width(3), .enable("false")) multiplexer_3 (
    .in0(rom_1_data[11:9]), .in1(3'b111), .out(multiplexer_3_out), .sel(JAL));
  Multiplexer #(.width(3), .enable("false")) multiplexer_4 (
    .in0(multiplexer_3_out), .in1(3'b001), .out(multiplexer_4_out), .sel(LUI));
  and and_1 (and_1_out, RTZ, MOVZ);
  and and_2 (and_2_out, ~RTZ, MOVN);  // AND_Gate
  File_Reg file_reg_1 (
    .RA(rom_1_data[8:6]), .RB(multiplexer_2_out), .RW(multiplexer_4_out), .RegWrite(or_1_out), .BusW(Result),
    .BusA(file_reg_1_busa), .BusB(file_reg_1_busb), .Clock(clock_1_out), .out_15(out_5), .out_14(out_7),
    .out_11(out_4), .out_10(out_2), .out_9(out_6), .out_8(out_3), .out_7(out_1));
  or or_1 (or_1_out, and_1_out, and_2_out, RegWr);
  MainCtrl_main main_1 (
    .in_1(rom_1_data_2), .in_2(func), .RT(RT), .RegWr(RegWr), .ExtOp(ExtOp), .ALUSrc(ALUSrc), .MemRd(MemRd),
    .MemWr(MemWr), .WBdata(WBdata), .JAL(JAL), .JALR(JALR), .Lui(LUI), .MOVZ(MOVZ), .MOVN(MOVN));
  extender extender_1 (.Imm6({rom_1_data[5:3], func}), .Imm16(Imm16), .ExtOp(ExtOp));
  Adder #(.width(12)) adder_2 (.a(register_1_q), .b(bit_extender_2_out), .out(adder_2_out));  // open: cin, cout
  assign bit_extender_2_out = {{6{rom_1_data[5]}}, {rom_1_data[5:3], func}};  // Bit_Extender bit_extender_2
  Comparator #(.width(16), .mode("unsigned")) comparator_1 (
    .a(file_reg_1_busb), .b({16{1'b0}}), .eq(RTZ));  // open: gt, lt
  Multiplexer #(.width(16), .enable("false")) multiplexer_5 (
    .in0(file_reg_1_busa), .in1(LUI_Imm12), .out(multiplexer_5_out), .sel(LUI));
  Multiplexer #(.width(16), .enable("false")) multiplexer_6 (
    .in0(file_reg_1_busb), .in1(Imm16), .out(multiplexer_6_out), .sel(ALUSrc));
  Multiplexer #(.width(16), .enable("false")) multiplexer_7 (
    .in0(multiplexer_8_out), .in1({16{1'b0}}), .out(multiplexer_7_out), .sel(MOVN));
  Multiplexer #(.width(16), .enable("false")) multiplexer_8 (
    .in0(multiplexer_6_out), .in1(16'h4), .out(multiplexer_8_out), .sel(LUI));
  ALUOp_main main_2 (.ALUOp(main_2_aluop), .in_2(rom_1_data_2), .func(func));
  ALU_main main_3 (
    .DATA_A(multiplexer_5_out), .DATA_B(multiplexer_7_out), .ALUOp(main_2_aluop), .GT(GT), .ZERO(Zero),
    .RESULT(main_3_result));
  assign bit_extender_3_out = {{4{1'b0}}, pc1};  // Bit_Extender bit_extender_3
  RAM #(.addrWidth(12), .dataWidth(16), .bus("separate")) ram_1 (
    .addr(main_3_result[11:0]), .din(file_reg_1_busb), .data(ram_1_data), .str(MemWr), .clk(clock_1_out),
    .ld(MemRd));  // open: sel, clr
  Multiplexer #(.width(16), .enable("false")) multiplexer_9 (
    .in0(main_3_result), .in1(ram_1_data), .out(multiplexer_9_out), .sel(WBdata));
  Multiplexer #(.width(16), .enable("false")) multiplexer_10 (
    .in0(multiplexer_9_out), .in1(bit_extender_3_out), .out(Result), .sel(or_2_out));
  or or_2 (or_2_out, JAL, JALR);

  // Other names for the same wires on the sheet: R1[15:0] = out_1; R2[15:0] = out_3; R3[15:0] = out_6;
  //   R4[15:0] = out_2; R5[15:0] = out_4; R6[15:0] = out_7; R7[15:0] = out_5

  // Notes on the sheet:
  //   PC = PC + 1
  //   PC = RS[11:0]
  //   PC = Branch Target
  //   PC = Imm12
  //   contents of rom_1 (hex, n*v repeats v):
  //   424f 4fd4 166d
  //   Op
  //   RD
  //   RT
  //   Imm12
  //   RS
  //   RT
  //   JAL
  //   LUI
  //   Imm6
  //   RegWr
  //   MemWr
  //   ALU Result
  //   MemRd
  //   WBData
endmodule

module File_Reg (
  input  [2:0] RA,
  input  [2:0] RB,
  input  [2:0] RW,
  input  RegWrite,
  input  Clock,
  input  [15:0] BusW,
  output [15:0] out_7,
  output [15:0] out_8,
  output [15:0] out_9,
  output [15:0] out_10,
  output [15:0] out_11,
  output [15:0] BusA,
  output [15:0] BusB,
  output [15:0] out_14,
  output [15:0] out_15
);

  wire and_1_out, and_2_out, and_3_out, and_4_out, and_5_out, and_6_out, and_7_out, decoder_1_out0,
       decoder_1_out1, decoder_1_out2, decoder_1_out3, decoder_1_out4, decoder_1_out5, decoder_1_out6,
       decoder_1_out7, decoder_2_out0, decoder_2_out1, decoder_2_out2, decoder_2_out3, decoder_2_out4,
       decoder_2_out5, decoder_2_out6, decoder_2_out7, decoder_3_out0, decoder_3_out1, decoder_3_out2,
       decoder_3_out3, decoder_3_out4, decoder_3_out5, decoder_3_out6, decoder_3_out7;

  Decoder #(.select(3), .enable("false")) decoder_1 (
    .out0(decoder_1_out0), .out1(decoder_1_out1), .out2(decoder_1_out2), .out3(decoder_1_out3),
    .out4(decoder_1_out4), .out5(decoder_1_out5), .out6(decoder_1_out6), .out7(decoder_1_out7), .sel(RW));
  and and_1 (and_1_out, decoder_1_out1, RegWrite);
  and and_2 (and_2_out, decoder_1_out2, RegWrite);
  and and_3 (and_3_out, decoder_1_out3, RegWrite);
  and and_4 (and_4_out, decoder_1_out4, RegWrite);
  and and_5 (and_5_out, decoder_1_out5, RegWrite);
  and and_6 (and_6_out, decoder_1_out6, RegWrite);
  and and_7 (and_7_out, decoder_1_out7, RegWrite);
  Register #(.width(16)) register_1 (.D(BusW), .en(and_1_out), .Q(out_7), .clk(Clock));  // open: clr
  Register #(.width(16)) register_2 (.D(BusW), .en(and_2_out), .Q(out_8), .clk(Clock));  // open: clr
  Register #(.width(16)) register_3 (.D(BusW), .en(and_3_out), .Q(out_9), .clk(Clock));  // open: clr
  Register #(.width(16)) register_4 (.D(BusW), .en(and_4_out), .Q(out_10), .clk(Clock));  // open: clr
  Register #(.width(16)) register_5 (.D(BusW), .en(and_5_out), .Q(out_11), .clk(Clock));  // open: clr
  Register #(.width(16)) register_6 (.D(BusW), .en(and_6_out), .Q(out_14), .clk(Clock));  // open: clr
  Register #(.width(16)) register_7 (.D(BusW), .en(and_7_out), .Q(out_15), .clk(Clock));  // open: clr
  Decoder #(.select(3), .enable("false")) decoder_2 (
    .out0(decoder_2_out0), .out1(decoder_2_out1), .out2(decoder_2_out2), .out3(decoder_2_out3),
    .out4(decoder_2_out4), .out5(decoder_2_out5), .out6(decoder_2_out6), .out7(decoder_2_out7), .sel(RA));
  assign BusA = decoder_2_out1 ? out_7 : 16'bz;  // Controlled_Buffer controlled_buffer_1
  assign BusA = decoder_2_out2 ? out_8 : 16'bz;  // Controlled_Buffer controlled_buffer_2
  assign BusA = decoder_2_out3 ? out_9 : 16'bz;  // Controlled_Buffer controlled_buffer_3
  assign BusA = decoder_2_out4 ? out_10 : 16'bz;  // Controlled_Buffer controlled_buffer_4
  assign BusA = decoder_2_out5 ? out_11 : 16'bz;  // Controlled_Buffer controlled_buffer_5
  assign BusA = decoder_2_out6 ? out_14 : 16'bz;  // Controlled_Buffer controlled_buffer_6
  assign BusA = decoder_2_out7 ? out_15 : 16'bz;  // Controlled_Buffer controlled_buffer_7
  assign BusA = decoder_2_out0 ? {16{1'b0}} : 16'bz;  // Controlled_Buffer controlled_buffer_8
  Decoder #(.select(3), .enable("false")) decoder_3 (
    .out0(decoder_3_out0), .out1(decoder_3_out1), .out2(decoder_3_out2), .out3(decoder_3_out3),
    .out4(decoder_3_out4), .out5(decoder_3_out5), .out6(decoder_3_out6), .out7(decoder_3_out7), .sel(RB));
  assign BusB = decoder_3_out2 ? out_8 : 16'bz;  // Controlled_Buffer controlled_buffer_9
  assign BusB = decoder_3_out3 ? out_9 : 16'bz;  // Controlled_Buffer controlled_buffer_10
  assign BusB = decoder_3_out4 ? out_10 : 16'bz;  // Controlled_Buffer controlled_buffer_11
  assign BusB = decoder_3_out5 ? out_11 : 16'bz;  // Controlled_Buffer controlled_buffer_12
  assign BusB = decoder_3_out6 ? out_14 : 16'bz;  // Controlled_Buffer controlled_buffer_13
  assign BusB = decoder_3_out7 ? out_15 : 16'bz;  // Controlled_Buffer controlled_buffer_14
  assign BusB = decoder_3_out0 ? {16{1'b0}} : 16'bz;  // Controlled_Buffer controlled_buffer_15
  assign BusB = decoder_3_out1 ? out_7 : 16'bz;  // Controlled_Buffer controlled_buffer_16
endmodule

module extender (
  input  [5:0] Imm6,
  input  ExtOp,
  output [15:0] Imm16
);

  wire [15:0] bit_extender_1_out, bit_extender_2_out;

  assign bit_extender_1_out = {{10{1'b0}}, Imm6};  // Bit_Extender bit_extender_1
  assign bit_extender_2_out = {{10{Imm6[5]}}, Imm6};  // Bit_Extender bit_extender_2
  Multiplexer #(.width(16), .enable("false")) multiplexer_1 (
    .in0(bit_extender_1_out), .in1(bit_extender_2_out), .out(Imm16), .sel(ExtOp));
endmodule

module pc_ctrl (
  input  [3:0] Op,
  input  in_2,
  input  in_3,
  input  [2:0] in_4,
  output [2:0] PCsrc
);

  wire _0, _2, _3, _4, _5, _6, _13, and_3_out, BEQ_out, BGE_out, BGT_out, BLE_out, BLT_out, BNE_out,
       decoder_1_out1, decoder_1_out7, decoder_1_out8, decoder_1_out9, decoder_1_out10, decoder_1_out11,
       decoder_1_out12, decoder_1_out14, decoder_1_out15, JALR, JALROUT, JR, JROUT, or_1_out, or_2_out,
       or_3_out, or_4_out;

  Decoder #(.select(4), .enable("false")) decoder_1 (
    .out0(_0), .out1(decoder_1_out1), .out2(_2), .out3(_3), .out4(_4), .out5(_5), .out6(_6),
    .out7(decoder_1_out7), .out8(decoder_1_out8), .out9(decoder_1_out9), .out10(decoder_1_out10),
    .out11(decoder_1_out11), .out12(decoder_1_out12), .out13(_13), .out14(decoder_1_out14),
    .out15(decoder_1_out15), .sel(Op));
  and and_1 (JR, ~in_4[0], in_4[1], in_4[2]);  // AND_Gate
  and and_2 (JALR, in_4[0], in_4[1], in_4[2]);
  or or_1 (or_1_out, in_2, in_3);
  and and_3 (and_3_out, ~in_2, ~in_3);  // AND_Gate
  and BNE (BNE_out, decoder_1_out7, ~in_2);  // AND_Gate
  and BEQ (BEQ_out, decoder_1_out8, in_2);
  and BGT (BGT_out, decoder_1_out9, in_3);
  and BGE (BGE_out, decoder_1_out10, or_1_out);
  and BLT (BLT_out, decoder_1_out11, and_3_out);
  and BLE (BLE_out, decoder_1_out12, ~in_3);  // AND_Gate
  or or_2 (or_2_out, decoder_1_out14, decoder_1_out15);
  or or_3 (or_3_out, BNE_out, BEQ_out, BGT_out, BGE_out, BLT_out, BLE_out);
  and and_4 (JROUT, decoder_1_out1, JR);
  and and_5 (JALROUT, decoder_1_out1, JALR);
  or or_4 (or_4_out, _0, _2, ~JROUT, ~JALROUT, _3, _4, _5, _6, _13);  // OR_Gate
  Priority_Encoder priority_encoder_1 (
    .in0(or_4_out), .in1(or_2_out), .in2(or_3_out), .in3(JROUT), .in4(JALROUT), .out(PCsrc));  // open: in5, in6, in7, en_in, gs, en_out

  // Other names for the same wires on the sheet: func[2:0] = in_4; GT = in_3; zero = in_2
endmodule
